# Fritzing sketch electronic_schematic (saved by Fritzing 0.9.9b)
breadboards: 1

parts:
  Part1 = Adafruit nRF52840 CLUE
  BATT1 = LiPoly Battery (1300mAh)
  BATT2 = LiPoly Battery (1300mAh)
  Part2 = Logic Level Converter
  J1 = Basic Servo
  U1 = TRANSISTOR_NPN_2 [package=to-92]
  L1 = Solenoid

nets:
  N1: Part1.D2/AIN4, U1.B
  N2: Part1.D9, Part2.TX_HV
  GND: Part1.GND, BATT1.negative, BATT2.negative, Part2.GND, J1.gnd, L1.pin1
  N3: Part1.VBAT, Part2.LV
  N4: BATT1.positive, BATT2.positive, Part2.HV, J1.vcc, U1.C
  N5: U1.E, L1.pin2

custom parts:
  LiPoly Battery (1300mAh): Lithium Ion Polymer Battery (1300mAh)
